# Fritzing sketch circuit (saved by Fritzing 0.8.7b)
breadboards: 1

parts:
  M1 = Stepper Motor - Bipolar  # not connected
  Power_plug1 = Power plug
  DRV_1 = DRV 8825 Stepper Motor Carrier, High Current [part_number="DRV 8825"]  # not connected
  DC1 = DC_DC_XL4016 [chip_label=XL4016 package=board_screw]  # not connected
  DC2 = DC_DC_XL4016 [package=board_screw]
  Raspberry_Pi_1 = Raspberry Pi 3 [part_number=RPI-3-V1.2]
  3-pins_Hall_Effect_Sensor1 = mystery part, 3 pins [chip_label="Hall Effect Sensor"]

nets:
  N1: Power_plug1.GND, DC2.IN-
  N2: Power_plug1.VCC, DC2.IN+
  N3: DC2.OUT+, DC2.OUT-, Raspberry_Pi_1.5V
  N4: Raspberry_Pi_1.3v3, 3-pins_Hall_Effect_Sensor1.pin3
  N5: Raspberry_Pi_1.GND, 3-pins_Hall_Effect_Sensor1.pin2
  N6: Raspberry_Pi_1.GIPO26, 3-pins_Hall_Effect_Sensor1.pin1

notes:
  12V
  5V
  3.3V

custom parts:
  DC_DC_XL4016: DC-DC Converter step down voltage regulator XL4016 custom sketch.
